# Fritzing sketch transmitter (saved by Fritzing 0.9.3b)

parts:
  Part1 = Arduino Uno (Rev3)
  Part4 = HMC5883L Triple-axis Magnetometer [part_number=1746]
  U1 = FS1000A - 433Mhz RF Transmitter [package=THT]

nets:
  N1: Part1.A5/SCL, Part4.SCL
  N2: Part1.D12/MISO, U1.DATA
  N3: Part1.A4/SDA, Part4.SDA
  5V: Part1.5V, Part4.3.3V, U1.VCC
  GND: Part1.GND, Part4.GND, U1.GND

custom parts:
  HMC5883L Triple-axis Magnetometer: A magnetometer can sense where the strongest magnetic force is coming from, generally used to detect magnetic north. We based this breakout on a popular and well loved magnetometer, the HMC5883L. This compact sensor uses I2C to communicate and its very easy to use. Since it's a 3.3V max chip, we added circuitry to make it 5V-safe logic and power, for easy use with either 3 or 5V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
  FS1000A - 433Mhz RF Transmitter: This is 433Mhz RF transmitter with receiver kit for Arduino ARM MCU wireless Application environment: Remote control switch, receiver module, motorcycles, automobile anti-theft products, home security products, electric doors, shutter doors, windows, remote control socket, remote control LED, remote audio remote control electric doors, garage door remote control, remote control retractable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
